# Fritzing sketch self driving sketch (saved by Fritzing 0.9.5d)
breadboards: 1

parts:
  Part1 = Arduino Uno (Rev3) - ICSP
  BC_556_transistor = PNP-Transistor [package="TO92 [THT]"]
  SP1 = SPEAKER [package=pcb_mount_speaker]
  R1 = Resistor [tolerance=±5% resistance=6700 package="2010 [SMD]"]
  microSD1 = MicroSD Card Module
  HC-SR04_Sensor_1 = HC-SR04 Ultrasonic Distance Sensor
  EDGY_motor_control1 = EDGY
  M1 = DC Motor
  M2 = DC Motor
  VCC1 = 4 x AAA Battery Mount

nets:
  VCC: Part1.5V, microSD1.VCC, HC-SR04_Sensor_1.VCC, EDGY_motor_control1.5V+
  N1: Part1.D8, HC-SR04_Sensor_1.TRIG
  N2: Part1.D9_PWM, R1.Pin_1
  N3: Part1.D10_PWM/SS, EDGY_motor_control1.Speed1
  N4: Part1.D11_PWM/MOSI, microSD1.MOSI
  N5: Part1.D12/MISO, microSD1.MISO
  N6: Part1.D13/SCK, microSD1.SCK
  GND: Part1.GND, BC_556_transistor.C, SP1.-, microSD1.GND, HC-SR04_Sensor_1.ECHO, EDGY_motor_control1.GND
  N7: Part1.D0/RX, EDGY_motor_control1.Speed2
  N8: Part1.D2, EDGY_motor_control1.A2
  N9: Part1.D3_PWM, EDGY_motor_control1.B2
  N10: Part1.D4, microSD1.CS
  N11: Part1.D5_PWM, HC-SR04_Sensor_1.GND
  N12: Part1.D6_PWM, EDGY_motor_control1.A1
  N13: Part1.D7, EDGY_motor_control1.B1
  N14: Part1.VIN, VCC1.-, VCC1.+
  N15: BC_556_transistor.E, SP1.+
  N16: BC_556_transistor.B, R1.Pin_0
  N17: EDGY_motor_control1.B2out, M2.pin_1
  N18: EDGY_motor_control1.A2out, M2.pin_2
  N19: EDGY_motor_control1.B1out, M1.pin_1
  N20: EDGY_motor_control1.A1out, M1.pin_2
